// Digital circuit Ejercicio 1.dig as structural Verilog
module Ejercicio_1 (
  input  D0,
  input  D1,
  input  D2,
  input  D3,
  input  D4,
  input  D5,
  input  D6,
  input  D7,
  input  Sel_2,
  input  Sel_1,
  input  Sel_0,
  output S
);

  wire and_1_out, and_2_out, and_3_out, and_4_out, and_5_out, and_6_out, and_7_out, and_8_out, not_1_out,
       not_2_out, not_3_out, or_1_out, or_2_out;

  not not_1 (not_1_out, Sel_2);
  not not_2 (not_2_out, Sel_1);
  not not_3 (not_3_out, Sel_0);
  and and_1 (and_1_out, D0, not_1_out, not_2_out, not_3_out);
  and and_2 (and_2_out, D1, not_1_out, not_2_out, Sel_0);
  and and_3 (and_3_out, D2, not_1_out, Sel_1, not_3_out);
  and and_4 (and_4_out, D3, not_1_out, Sel_1, Sel_0);
  and and_5 (and_5_out, D4, Sel_2, not_2_out, not_3_out);
  and and_6 (and_6_out, D5, Sel_2, not_2_out, Sel_0);
  and and_7 (and_7_out, D6, Sel_2, Sel_1, not_3_out);
  and and_8 (and_8_out, D7, Sel_2, Sel_1, Sel_0);
  or or_1 (or_1_out, and_1_out, and_2_out, and_3_out, and_4_out);
  or or_2 (or_2_out, and_5_out, and_6_out, and_7_out, and_8_out);
  or or_3 (S, or_1_out, or_2_out);

  // Notes on the sheet:
  //   Multiplexor 8 entradas
  //   Sel 2 : 0
  //   Sel 2 : 1
  //   Sel 1 : 1
  //   Sel 1 : 0
  //   Sel 0 : 0
endmodule
