// Digital circuit Ejercicio 2.dig as structural Verilog
module Ejercicio_2 (
  input  Entrada,
  input  Sel_0,
  input  Sel_1,
  output S0,
  output S1,
  output S2,
  output S3
);

  wire not_1_out, not_2_out;

  not not_1 (not_1_out, Sel_1);
  not not_2 (not_2_out, Sel_0);
  and and_1 (S0, Entrada, not_1_out, not_2_out);
  and and_2 (S1, Entrada, not_1_out, Sel_0);
  and and_3 (S2, Entrada, Sel_1, not_2_out);
  and and_4 (S3, Entrada, Sel_1, Sel_0);

  // Notes on the sheet:
  //   Demultiplexor
  //   Sel 1 : 1
  //   Sel 0 : 1
  //   Sel 1 : 0
  //   Sel 0 : 0
endmodule
