// Digital circuit Ejercicio 3 - flip flop JK.dig as structural Verilog
module Ejercicio_3___flip_flop_JK (
  input  Clock,
  input  K,
  input  J,
  output Q
);

  wire nand_1_out, nand_2_out, nand_3_out, nand_4_out, nand_5_out, nand_6_out, nand_8_out, not_1_out;

  not not_1 (not_1_out, Clock);
  nand nand_1 (nand_1_out, J, nand_8_out, Clock);
  nand nand_2 (nand_2_out, Clock, Q, K);
  nand nand_3 (nand_3_out, nand_1_out, nand_4_out);
  nand nand_4 (nand_4_out, nand_3_out, nand_2_out);
  nand nand_5 (nand_5_out, nand_3_out, not_1_out);
  nand nand_6 (nand_6_out, not_1_out, nand_4_out);
  nand nand_7 (Q, nand_5_out, nand_8_out);
  nand nand_8 (nand_8_out, Q, nand_6_out);

  // Notes on the sheet:
  //   Flanco de subida
  //   Funcianomiento del flip flop JK :
  //   - Cuando encendemos J, la salida Q se enciende (si ya no era encendida). 
  //   - Cuando encendemos K, la salida Q se apaga (si ya no era apagada).
  //   - Apagar S o R no cambia por nada la salida Q. 
  //   - Cuando las entradas S y R estan encendidas en el mismo tiempo, la salida Q se enciende
  //    y se apaga por turnos. La inestabilidad del flip flip RS esta resolvada. El flip flop JK funciona con 
  //   un sistema que llamamos "maestro/esclavo", lo que quiere decir que los cambios de estado se 
  //   hacen en dos etapas.
  //   Flip Flop JK
  //   Flanco de bajada
endmodule
