// Digital circuit Ejercicio 3 - flip flop RS.dig as structural Verilog
module Ejercicio_3___flip_flop_RS (
  input  Clock,
  input  R,
  input  S,
  output Q
);

  wire nand_1_out, nand_2_out, nand_4_out;

  nand nand_1 (nand_1_out, S, Clock);
  nand nand_2 (nand_2_out, Clock, R);
  nand nand_3 (Q, nand_1_out, nand_4_out);
  nand nand_4 (nand_4_out, Q, nand_2_out);

  // Notes on the sheet:
  //   Flanco de subida
  //   Funcianomiento del flip flop RS :
  //   En cada flanco de subida del reloj, el sistema se actualiza de la manera siguiente :
  //   - Cuando encendemos S, la salida Q se enciende (si ya no era encendida). 
  //   - Cuando encendemos R, la salida Q se apaga (si ya no era apagada).
  //   - Apagar S o R no cambia por nada la salida Q. 
  //   - Las entradas S y R no pueden estar encendidas en el mismo tiempo. Esto causa insestabilidad.
  //   Flip Flop RS
endmodule
