// Digital circuit Ejercicio 4 - Registro 4 bits.dig as structural Verilog
module Ejercicio_4___Registro_4_bits (
  input  Config_PIN_3,
  input  Set,
  input  Config_PIN_2,
  input  Config_PIN_1,
  input  Config_PIN_0,
  input  Set_2,
  input  Set_3,
  input  Enable,
  input  Clock,
  input  Data_de_salida_0,
  input  Data_de_entrada_0,
  input  Clear,
  input  Set_4,
  input  Set_5,
  input  Data_de_salida_1,
  input  Data_de_entrada_1,
  input  Set_6,
  input  Set_7,
  input  Data_de_salida_2,
  input  Data_de_entrada_2,
  input  Set_8,
  input  Set_9,
  input  Data_de_salida_3,
  input  Data_de_entrada_3,
  output PIN_0_IN,
  output PIN_0_OUT,
  output PIN_1_IN,
  output PIN_1_OUT,
  output PIN_2_IN,
  output PIN_2_OUT,
  output PIN_3_IN,
  output PIN_3_OUT
);

  wire C0, C1, C2, C3, driver_1_out, driver_2_out, driver_3_out, driver_4_out, driverinvsel_1_out,
       driverinvsel_2_out, driverinvsel_3_out, driverinvsel_4_out, multiplexer_1_out, multiplexer_2_out,
       multiplexer_3_out, multiplexer_4_out, multiplexer_5_out, multiplexer_6_out, multiplexer_7_out,
       multiplexer_8_out, multiplexer_9_out, multiplexer_10_out, multiplexer_11_out, multiplexer_12_out,
       not_1_out, not_2_out, not_3_out, not_4_out;

  Multiplexer multiplexer_1 (.sel(Enable), .in_0(C3), .in_1(Config_PIN_3), .out(multiplexer_1_out));
  D_FF_AS d_ff_as_1 (.Set(Set), .D(multiplexer_1_out), .C(Clock), .Clr(Clear), .Q(C3));  // open: nQ
  Multiplexer multiplexer_2 (.sel(Enable), .in_0(C2), .in_1(Config_PIN_2), .out(multiplexer_2_out));
  D_FF_AS d_ff_as_2 (.Set(Set), .D(multiplexer_2_out), .C(Clock), .Clr(Clear), .Q(C2));  // open: nQ
  Multiplexer multiplexer_3 (.sel(Enable), .in_0(C1), .in_1(Config_PIN_1), .out(multiplexer_3_out));
  D_FF_AS d_ff_as_3 (.Set(Set), .D(multiplexer_3_out), .C(Clock), .Clr(Clear), .Q(C1));  // open: nQ
  Multiplexer multiplexer_4 (.sel(Enable), .in_0(C0), .in_1(Config_PIN_0), .out(multiplexer_4_out));
  D_FF_AS d_ff_as_4 (.Set(Set), .D(multiplexer_4_out), .C(Clock), .Clr(Clear), .Q(C0));  // open: nQ
  assign driver_1_out = C0 ? Data_de_entrada_0 : 1'bz;  // Driver driver_1
  assign driverinvsel_1_out = ~C0 ? Data_de_salida_0 : 1'bz;  // DriverInvSel driverinvsel_1
  assign driver_2_out = C1 ? Data_de_entrada_1 : 1'bz;  // Driver driver_2
  assign driverinvsel_2_out = ~C1 ? Data_de_salida_1 : 1'bz;  // DriverInvSel driverinvsel_2
  Multiplexer multiplexer_5 (.sel(Enable), .in_0(PIN_0_IN), .in_1(driver_1_out), .out(multiplexer_5_out));
  Multiplexer multiplexer_6 (.sel(Enable), .in_0(PIN_0_OUT), .in_1(driverinvsel_1_out), .out(multiplexer_6_out));
  Multiplexer multiplexer_7 (.sel(Enable), .in_0(PIN_1_IN), .in_1(driver_2_out), .out(multiplexer_7_out));
  Multiplexer multiplexer_8 (.sel(Enable), .in_0(PIN_1_OUT), .in_1(driverinvsel_2_out), .out(multiplexer_8_out));
  not not_1 (not_1_out, C0);
  not not_2 (not_2_out, C1);
  D_FF_AS d_ff_as_5 (.Set(Set_2), .D(multiplexer_5_out), .C(Clock), .Clr(not_1_out), .Q(PIN_0_IN));  // open: nQ
  D_FF_AS d_ff_as_6 (.Set(Set_3), .D(multiplexer_6_out), .C(Clock), .Clr(C0), .Q(PIN_0_OUT));  // open: nQ
  D_FF_AS d_ff_as_7 (.Set(Set_4), .D(multiplexer_7_out), .C(Clock), .Clr(not_2_out), .Q(PIN_1_IN));  // open: nQ
  D_FF_AS d_ff_as_8 (.Set(Set_5), .D(multiplexer_8_out), .C(Clock), .Clr(C1), .Q(PIN_1_OUT));  // open: nQ
  assign driver_3_out = C2 ? Data_de_entrada_2 : 1'bz;  // Driver driver_3
  assign driverinvsel_3_out = ~C2 ? Data_de_salida_2 : 1'bz;  // DriverInvSel driverinvsel_3
  assign driver_4_out = C3 ? Data_de_entrada_3 : 1'bz;  // Driver driver_4
  assign driverinvsel_4_out = ~C3 ? Data_de_salida_3 : 1'bz;  // DriverInvSel driverinvsel_4
  Multiplexer multiplexer_9 (.sel(Enable), .in_0(PIN_2_IN), .in_1(driver_3_out), .out(multiplexer_9_out));
  Multiplexer multiplexer_10 (.sel(Enable), .in_0(PIN_2_OUT), .in_1(driverinvsel_3_out), .out(multiplexer_10_out));
  Multiplexer multiplexer_11 (.sel(Enable), .in_0(PIN_3_IN), .in_1(driver_4_out), .out(multiplexer_11_out));
  Multiplexer multiplexer_12 (.sel(Enable), .in_0(PIN_3_OUT), .in_1(driverinvsel_4_out), .out(multiplexer_12_out));
  not not_3 (not_3_out, C2);
  not not_4 (not_4_out, C3);
  D_FF_AS d_ff_as_9 (.Set(Set_6), .D(multiplexer_9_out), .C(Clock), .Clr(not_3_out), .Q(PIN_2_IN));  // open: nQ
  D_FF_AS d_ff_as_10 (.Set(Set_7), .D(multiplexer_10_out), .C(Clock), .Clr(C2), .Q(PIN_2_OUT));  // open: nQ
  D_FF_AS d_ff_as_11 (.Set(Set_8), .D(multiplexer_11_out), .C(Clock), .Clr(not_4_out), .Q(PIN_3_IN));  // open: nQ
  D_FF_AS d_ff_as_12 (.Set(Set_9), .D(multiplexer_12_out), .C(Clock), .Clr(C3), .Q(PIN_3_OUT));  // open: nQ

  // Notes on the sheet:
  //   Registro 4 bits CONFIGURACION
  //   Config PIN :
  //   0 --> salida
  //   1 --> entrada
  //   PIN I/O
  //   PIN 0
  //   PIN 1
  //   Registro que almanece el estado del pin configurado como entrada
  //   Registro que controla el estado del pin configurado como salida
  //   Con este sistema, los Clear deben estar forzados 
  //   para que el pin se apaga cuando la configuracion cambia...
  //   PIN 2
  //   PIN 3
endmodule
